# Fritzing sketch PowerCtrl (saved by Fritzing 0.9.2b)
breadboards: 1

parts:
  U1 = attiny85 [package=dip]
  R2 = Resistor [tolerance=±5% resistance=10k package=THT]
  R1 = PHOTOCELL [package=photocell]
  R3 = Trimmer Potentiometer [maximum_resistance=10kΩ package=THT]
  C1 = Electrolytic Capacitor [capacitance=10µF package="100 mil [THT, electrolytic]"]
  S1 = Pushbutton [package=THT]
  D1 = Schottky Diode [part_number=1N5817 package="300 mil [THT]"]

nets:
  N1: U1.Pin_2, R2.Pin_0, R1.P$2, D1.anode
  GND: U1.Pin_4, R1.P$1, C1.-, S1.leg0
  Output: U1.Pin_5
  5V: U1.Pin_8, R3.leg2
  N2: R2.Pin_1, R3.leg1, R3.wiper
  to PowerBtn: D1.cathode

notes:
  PowerCtrl, 1.2
